# Fritzing sketch Untitled Sketch (saved by Fritzing 0.9.5d)

parts:
  LED1 = LED - 5mm [color="Red (633nm)" package="5 mm [THT]"]
  R1 = Resistor [tolerance=±5% resistance=220 package=THT]
  LED2 = LED - 5mm [color="Green (570nm)" package="5 mm [THT]"]
  R2 = Resistor [tolerance=±5% resistance=220 package=THT]
  U1 = ESP32-38PinWide [part_number=ESP32-38PinWide]
  J1 = Basic Servo
  hc-sr1 = hc-sr04

nets:
  GND: LED1.cathode, LED2.cathode, U1.GND, J1.gnd
  N1: R1.Pin_1, U1.GPIO2
  N2: R2.Pin_1, U1.GPIO4
  N3: U1.3.3, hc-sr1.VCC
  N4: U1.GPIO5, J1.pulse
  N5: U1.GPIO18, hc-sr1.Trig
  N6: U1.GPIO19, hc-sr1.Echo

custom parts:
  ESP32-38PinWide: Generic 38-Pin ESP32 with wide format (only access to one side of pins on a breadboard) based on Stephen Lilley's HiLetgo ESP-WROOM-32 ESP32 ESP-32S Development Board.
