# Fritzing sketch Untitled Sketch (saved by Fritzing 0.9.5d)

parts:
  U1 = ESP32-38PinWide [part_number=ESP32-38PinWide]
  J1 = Basic Servo
  PIR1 = PIR sensor
  R1 = Resistor [tolerance=±5% resistance=220 package=THT]
  R2 = Resistor [tolerance=±5% resistance=220 package=THT]
  LED1 = LED - 5mm [color="Orange (612nm)" package="5 mm [THT]"]
  LED2 = LED - 5mm [color="Red (633nm)" package="5 mm [THT]"]  # not connected

nets:
  N1: U1.3.3, J1.vcc
  N2: U1.GPIO14, PIR1.SIG
  N3: U1.GPIO11, J1.gnd
  N4: U1.GPIO2, R2.Pin_1
  N5: U1.GPIO4, R1.Pin_1
  N6: U1.GPIO5, J1.pulse
  N7: U1.GND, LED1.cathode

custom parts:
  ESP32-38PinWide: Generic 38-Pin ESP32 with wide format (only access to one side of pins on a breadboard) based on Stephen Lilley's HiLetgo ESP-WROOM-32 ESP32 ESP-32S Development Board.
